// Logisim project SimpleTon_Design.circ as structural Verilog: 7 circuits, main circuit main
module main (
  input  Clear_Memory
);

  wire commandline_sender_1__3, commandline_sender_1__4, commandline_sender_1__6, commandline_sender_1__7,
       commandline_sender_1__8, commandline_sender_1__9, commandline_sender_1__12, commandline_sender_1__13,
       commandline_sender_1_vselect, decoder_1_out0, decoder_1_out1, decoder_1_out2, decoder_1_out3,
       decoder_2_out0, decoder_2_out1, not_1_out, or_1_out, or_2_out, Step_out;
  wire [1:0] commandline_sender_1_oper, commandline_sender_1_rselect, priority_encoder_1_out, ram_1_data_2,
       ram_1_data_4;
  wire [7:0] commandline_sender_1_value_2, Core_q, counter_1_q, demultiplexer_1_out0, demultiplexer_1_out1,
       double_sided_multiplexer_1_lowero, double_sided_multiplexer_1_uppero0,
       double_sided_multiplexer_1_uppero1, double_sided_multiplexer_1_uppero2,
       double_sided_multiplexer_1_uppero3, MC_q, multiplexer_1_out, multiplexer_2_out, n8_bit_alu_1_output,
       n8_bit_enabler_1_o, n8_bit_enabler_2_o, R0_q, R1_q, R2_q, R3_q, ram_1_data, V1_q, V2_q;
  wire [15:10] ram_1_data_3;

  Button Step (.out(Step_out));
  Decoder #(.select(2), .enable("false")) decoder_1 (
    .out0(decoder_1_out0), .out1(decoder_1_out1), .out2(decoder_1_out2), .out3(decoder_1_out3),
    .sel(commandline_sender_1_rselect));
  not not_1 (not_1_out, Step_out);
  Register #(.trigger("high")) R0 (
    .D(double_sided_multiplexer_1_uppero0), .en(decoder_1_out0), .Q(R0_q), .clk(1'b1));  // open: clr
  _8_bit_Enabler u_8_bit_enabler_1 (.I(commandline_sender_1_value_2), .Enable(or_1_out), .O(n8_bit_enabler_1_o));
  Priority_Encoder #(.select(2)) priority_encoder_1 (
    .in0(commandline_sender_1__12), .in1(commandline_sender_1__8), .in2(commandline_sender_1__3),
    .in3(commandline_sender_1__7), .out(priority_encoder_1_out));  // open: gs, en_out, en_in
  Counter counter_1 (
    .load(not_1_out), .D(MC_q), .count(Step_out), .Q(counter_1_q), .clk(or_2_out));  // open: carry, clr
  Register #(.trigger("high")) R1 (
    .D(double_sided_multiplexer_1_uppero1), .en(decoder_1_out1), .Q(R1_q), .clk(1'b1));  // open: clr
  Multiplexer #(.select(2), .width(8), .enable("false")) multiplexer_1 (
    .in0(n8_bit_enabler_1_o), .in1(n8_bit_alu_1_output), .in2(double_sided_multiplexer_1_lowero), .in3(MC_q),
    .out(multiplexer_1_out), .sel(priority_encoder_1_out));
  or or_1 (or_1_out, commandline_sender_1__7, commandline_sender_1__12, commandline_sender_1__3, commandline_sender_1__8);
  Multiplexer #(.width(8), .enable("false")) multiplexer_2 (
    .in0(counter_1_q), .in1(Core_q), .out(multiplexer_2_out), .sel(commandline_sender_1__6));
  or or_2 (or_2_out, commandline_sender_1__6, Step_out);
  Register #(.trigger("high")) R2 (
    .D(double_sided_multiplexer_1_uppero2), .en(decoder_1_out2), .Q(R2_q), .clk(1'b1));  // open: clr
  Double_Sided_Multiplexer double_sided_multiplexer_1 (
    .RSelect(commandline_sender_1_rselect), .ptCfR(commandline_sender_1__3), .pfCtR(commandline_sender_1__4),
    .UpperI0(R0_q), .UpperO0(double_sided_multiplexer_1_uppero0), .UpperI1(R1_q),
    .UpperO1(double_sided_multiplexer_1_uppero1), .UpperI2(R2_q),
    .UpperO2(double_sided_multiplexer_1_uppero2), .UpperI3(R3_q),
    .UpperO3(double_sided_multiplexer_1_uppero3), .LowerO(double_sided_multiplexer_1_lowero), .LowerI(Core_q));
  Register #(.trigger("high")) Core (.D(multiplexer_1_out), .en(or_1_out), .Q(Core_q), .clk(1'b1));  // open: clr
  Register #(.trigger("high")) MC (.D(multiplexer_2_out), .en(or_2_out), .Q(MC_q), .clk(1'b1));  // open: clr
  Register #(.trigger("high")) R3 (
    .D(double_sided_multiplexer_1_uppero3), .en(decoder_1_out3), .Q(R3_q), .clk(1'b1));  // open: clr
  _8_bit_Enabler u_8_bit_enabler_2 (.I(Core_q), .Enable(commandline_sender_1__13), .O(n8_bit_enabler_2_o));
  Demultiplexer #(.width(8)) demultiplexer_1 (
    .out0(demultiplexer_1_out0), .out1(demultiplexer_1_out1), .in(Core_q),
    .sel(commandline_sender_1_vselect), .en(commandline_sender_1__9));
  Decoder decoder_2 (
    .out0(decoder_2_out0), .out1(decoder_2_out1), .sel(commandline_sender_1_vselect),
    .en(commandline_sender_1__9));
  CommandLine_Sender commandline_sender_1 (
    ._13(commandline_sender_1__13), ._12(commandline_sender_1__12), ._7(commandline_sender_1__7),
    ._3(commandline_sender_1__3), ._8(commandline_sender_1__8), ._6(commandline_sender_1__6),
    ._4(commandline_sender_1__4), ._9(commandline_sender_1__9), .Oper(commandline_sender_1_oper),
    .VSelect(commandline_sender_1_vselect), .RSelect(commandline_sender_1_rselect),
    .Value_2(commandline_sender_1_value_2), .A(ram_1_data_3[15]), .B(ram_1_data_3[14]), .C(ram_1_data_3[13]),
    .O(ram_1_data_4), .V(ram_1_data_3[10]), .R(ram_1_data_2), .Value(ram_1_data));
  Register #(.trigger("high")) V1 (.D(demultiplexer_1_out0), .en(decoder_2_out0), .Q(V1_q), .clk(1'b1));  // open: clr
  Register #(.trigger("high")) V2 (.D(demultiplexer_1_out1), .en(decoder_2_out1), .Q(V2_q), .clk(1'b1));  // open: clr
  _8_bit_ALU u_8_bit_alu_1 (
    .A(V1_q), .B(V2_q), .Output(n8_bit_alu_1_output), .Oper(commandline_sender_1_oper),
    .Enable(commandline_sender_1__8));
  Hex_Digit_Display hex_digit_display_1 (.value(R3_q[7:4]));  // open: dp
  Hex_Digit_Display hex_digit_display_2 (.value(R3_q[3:0]));  // open: dp
  RAM #(.dataWidth(16), .bus("separate")) ram_1 (
    .addr(MC_q), .din({{8{1'b0}}, n8_bit_enabler_2_o}),
    .data({ram_1_data_3[15:13], ram_1_data_4, ram_1_data_3[10], ram_1_data_2, ram_1_data}),
    .str(commandline_sender_1__13), .clk(or_2_out), .ld(1'b1), .clr(Clear_Memory));  // open: sel

  // Notes on the sheet:
  //   address to give to memory for reading
  //   Enable write ro memory
  //   Value to be written to memory (LSB)
endmodule

// DSMUX
module Double_Sided_Multiplexer (
  input  [7:0] UpperI0,
  input  [7:0] UpperI1,
  input  [7:0] UpperI2,
  input  [7:0] UpperI3,
  input  [1:0] RSelect,
  input  ptCfR,
  input  pfCtR,
  input  [7:0] LowerI,
  output [7:0] UpperO0,
  output [7:0] UpperO1,
  output [7:0] UpperO2,
  output [7:0] UpperO3,
  output [7:0] LowerO
);

  Multiplexer #(.select(2), .width(8)) multiplexer_1 (
    .in0(UpperI0), .in1(UpperI1), .in2(UpperI2), .in3(UpperI3), .out(LowerO), .sel(RSelect), .en(ptCfR));
  Demultiplexer #(.select(2), .width(8)) demultiplexer_1 (
    .out0(UpperO0), .out1(UpperO1), .out2(UpperO2), .out3(UpperO3), .in(LowerI), .sel(RSelect), .en(pfCtR));
endmodule

// ALU
module _8_bit_ALU (
  input  Enable,
  input  [7:0] A,
  input  [7:0] B,
  input  [1:0] Oper,
  output [7:0] Output
);

  wire [7:0] adder_1_out, and_1_out, or_1_out, subtractor_1_out;

  Adder adder_1 (.a(A), .b(B), .out(adder_1_out));  // open: cin, cout
  Subtractor subtractor_1 (.a(A), .b(B), .out(subtractor_1_out));  // open: bin, bout
  assign and_1_out = A & B;  // AND_Gate and_1, 8 bits wide
  assign or_1_out = A | B;  // OR_Gate or_1, 8 bits wide
  Multiplexer #(.select(2), .width(8)) multiplexer_1 (
    .in0(adder_1_out), .in1(subtractor_1_out), .in2(and_1_out), .in3(or_1_out), .out(Output), .sel(Oper),
    .en(Enable));
endmodule

// E
module _8_bit_Enabler (
  input  [7:0] I,
  input  Enable,
  output [7:0] O
);

  and and_1 (O[0], Enable, I[0]);
  and and_2 (O[1], Enable, I[1]);
  and and_3 (O[2], Enable, I[2]);
  and and_4 (O[3], Enable, I[3]);
  and and_5 (O[4], Enable, I[4]);
  and and_6 (O[5], Enable, I[5]);
  and and_7 (O[6], Enable, I[6]);
  and and_8 (O[7], Enable, I[7]);
endmodule

module test (
  input  in_1,
  input  [7:0] in_2,
  input  in_3,
  input  in_4
);

  Counter counter_1 (.load(in_1), .D(in_2), .count(in_3), .clk(in_4));  // open: Q, carry, clr
endmodule

// CommandLine
module CommandLine_Sender (
  input  A,
  input  B,
  input  C,
  input  [1:0] O,
  input  V,
  input  [1:0] R,
  input  [7:0] Value,
  output _13,
  output _12,
  output _7,
  output _3,
  output _8,
  output _6,
  output _4,
  output _9,
  output [1:0] Oper,
  output VSelect,
  output [1:0] RSelect,
  output [7:0] Value_2
);

  Decoder #(.select(3), .enable("false")) decoder_1 (
    .out0(_13), .out1(_12), .out2(_7), .out3(_3), .out4(_8), .out5(_6), .out6(_4), .out7(_9), .sel({A, B, C}));

  assign Oper = O;
  assign RSelect = R;
  assign Value_2 = Value;
  assign VSelect = V;
endmodule

module CPU_without_the_CommandLine (
  input  _3__ptCfR,
  input  _4__pfCtR,
  input  [1:0] _5__RSelect,
  input  _13__pfCtML,
  input  _8__ptCfV,
  input  [7:0] _2__Value,
  input  _1__EwtC,
  input  _12__ptCfIn,
  input  _9__pfCtV,
  input  _10__VSelect,
  input  [1:0] _11__Oper,
  input  _7__ptCfMC,
  input  _6__pfCtMC
);

  wire decoder_1_out0, decoder_1_out1, decoder_1_out2, decoder_1_out3, decoder_2_out0, decoder_2_out1,
       not_1_out, or_1_out, Step_out;
  wire [1:0] priority_encoder_1_out;
  wire [7:0] Core_q, counter_1_q, demultiplexer_1_out0, demultiplexer_1_out1,
       double_sided_multiplexer_1_lowero, double_sided_multiplexer_1_uppero0,
       double_sided_multiplexer_1_uppero1, double_sided_multiplexer_1_uppero2,
       double_sided_multiplexer_1_uppero3, MC_q, multiplexer_1_out, multiplexer_2_out, n8_bit_alu_1_output,
       n8_bit_enabler_1_o, R0_q, R1_q, R2_q, R3_q, V1_q, V2_q;

  Button Step (.out(Step_out));
  Decoder #(.select(2), .enable("false")) decoder_1 (
    .out0(decoder_1_out0), .out1(decoder_1_out1), .out2(decoder_1_out2), .out3(decoder_1_out3),
    .sel(_5__RSelect));
  not not_1 (not_1_out, Step_out);
  Register #(.trigger("high")) R0 (
    .D(double_sided_multiplexer_1_uppero0), .en(decoder_1_out0), .Q(R0_q), .clk(1'b1));  // open: clr
  Priority_Encoder #(.select(2)) priority_encoder_1 (
    .in0(_12__ptCfIn), .in1(_8__ptCfV), .in2(_3__ptCfR), .in3(_7__ptCfMC), .out(priority_encoder_1_out));  // open: gs, en_out, en_in
  Counter counter_1 (
    .load(not_1_out), .D(MC_q), .count(Step_out), .Q(counter_1_q), .clk(or_1_out));  // open: carry, clr
  Register #(.trigger("high")) R1 (
    .D(double_sided_multiplexer_1_uppero1), .en(decoder_1_out1), .Q(R1_q), .clk(1'b1));  // open: clr
  Multiplexer #(.select(2), .width(8), .enable("false")) multiplexer_1 (
    .in0(_2__Value), .in1(n8_bit_alu_1_output), .in2(double_sided_multiplexer_1_lowero), .in3(MC_q),
    .out(multiplexer_1_out), .sel(priority_encoder_1_out));
  Multiplexer #(.width(8), .enable("false")) multiplexer_2 (
    .in0(counter_1_q), .in1(Core_q), .out(multiplexer_2_out), .sel(_6__pfCtMC));
  or or_1 (or_1_out, _6__pfCtMC, Step_out);
  Register #(.trigger("high")) R2 (
    .D(double_sided_multiplexer_1_uppero2), .en(decoder_1_out2), .Q(R2_q), .clk(1'b1));  // open: clr
  Double_Sided_Multiplexer double_sided_multiplexer_1 (
    .RSelect(_5__RSelect), .ptCfR(_3__ptCfR), .pfCtR(_4__pfCtR), .UpperI0(R0_q),
    .UpperO0(double_sided_multiplexer_1_uppero0), .UpperI1(R1_q),
    .UpperO1(double_sided_multiplexer_1_uppero1), .UpperI2(R2_q),
    .UpperO2(double_sided_multiplexer_1_uppero2), .UpperI3(R3_q),
    .UpperO3(double_sided_multiplexer_1_uppero3), .LowerO(double_sided_multiplexer_1_lowero), .LowerI(Core_q));
  Register #(.trigger("high")) Core (.D(multiplexer_1_out), .en(_1__EwtC), .Q(Core_q), .clk(1'b1));  // open: clr
  Register #(.trigger("high")) MC (.D(multiplexer_2_out), .en(or_1_out), .Q(MC_q), .clk(1'b1));  // open: clr
  Register #(.trigger("high")) R3 (
    .D(double_sided_multiplexer_1_uppero3), .en(decoder_1_out3), .Q(R3_q), .clk(1'b1));  // open: clr
  _8_bit_Enabler u_8_bit_enabler_1 (.I(Core_q), .Enable(_13__pfCtML), .O(n8_bit_enabler_1_o));
  Demultiplexer #(.width(8)) demultiplexer_1 (
    .out0(demultiplexer_1_out0), .out1(demultiplexer_1_out1), .in(Core_q), .sel(_10__VSelect), .en(_9__pfCtV));
  Decoder decoder_2 (.out0(decoder_2_out0), .out1(decoder_2_out1), .sel(_10__VSelect), .en(_9__pfCtV));
  Register #(.trigger("high")) V1 (.D(demultiplexer_1_out0), .en(decoder_2_out0), .Q(V1_q), .clk(1'b1));  // open: clr
  Register #(.trigger("high")) V2 (.D(demultiplexer_1_out1), .en(decoder_2_out1), .Q(V2_q), .clk(1'b1));  // open: clr
  _8_bit_ALU u_8_bit_alu_1 (.A(V1_q), .B(V2_q), .Output(n8_bit_alu_1_output), .Oper(_11__Oper), .Enable(_8__ptCfV));
  Hex_Digit_Display hex_digit_display_1 (.value(R3_q[3:0]));  // open: dp
  Hex_Digit_Display hex_digit_display_2 (.value(R3_q[7:4]));  // open: dp
endmodule
